# Fritzing sketch v2.0 (saved by Fritzing 1.0.1rc)
breadboards: 1

parts:
  U1 = ESP32S-HiLetgo [part_number=ESP32S-HiLetgo]
  Adafruit_INA3221_-_Triple_0-26_VDC_±3_2_Amp_Power_Monitor_-_STEMMA_QT_/_Qwiic1 = Adafruit INA3221 - Triple 0-26 VDC, ±3.2 Amp Power Monitor - STEMMA QT / Qwiic [part_number=#6062]
  GY-NEO6MV1 = GY-NEO6MV2
  Componente1 = Solar Cell
  Componente2 = Solar Cell
  R1 = TRIMPOT [knob_status=50% package=3386u]
  R2 = TRIMPOT [knob_status=50% package=3386u]
  U2 = Sharp PC817 [package=THT]
  U3 = Sharp PC817 [package=THT]
  R3 = Resistor [tolerance=±5% resistance=220 package="0805 [SMD]"]
  R4 = Resistor [tolerance=±5% resistance=220 package="0805 [SMD]"]
  R5 = Resistor [tolerance=±5% power=0.25 resistance=4.7k package=THT]
  R6 = Resistor [tolerance=±5% power=0.25 resistance=4.7k package=THT]
  Componente3 = Lilypad Power Supply
  J1 = Basic Servo
  J2 = Basic Servo

nets:
  VCC: U1.3.3, Adafruit_INA3221_-_Triple_0-26_VDC_±3_2_Amp_Power_Monitor_-_STEMMA_QT_/_Qwiic1.VCC, GY-NEO6MV1.Vcc
  GND: U1.GND, Adafruit_INA3221_-_Triple_0-26_VDC_±3_2_Amp_Power_Monitor_-_STEMMA_QT_/_Qwiic1.GND, GY-NEO6MV1.GND, Componente1.-, Componente2.-, R1.WIPER, R2.WIPER, U3.Pin_1, R3.Pin_1, R4.Pin_1
  N1: U1.GPIO16, GY-NEO6MV1.Tx
  N2: U1.GPIO17, GY-NEO6MV1.Rx
  N3: U1.GPIO19, U2.Pin_1
  N4: Adafruit_INA3221_-_Triple_0-26_VDC_±3_2_Amp_Power_Monitor_-_STEMMA_QT_/_Qwiic1.VIN+1, Componente2.+
  N5: Adafruit_INA3221_-_Triple_0-26_VDC_±3_2_Amp_Power_Monitor_-_STEMMA_QT_/_Qwiic1.VIN+2, Componente1.+
  N6: Adafruit_INA3221_-_Triple_0-26_VDC_±3_2_Amp_Power_Monitor_-_STEMMA_QT_/_Qwiic1.VIN-2, R2.CW
  N7: Adafruit_INA3221_-_Triple_0-26_VDC_±3_2_Amp_Power_Monitor_-_STEMMA_QT_/_Qwiic1.VIN-1, R1.CW
  N8: U2.Pin_2, R3.Pin_0
  N9: U2.Pin_4, R6.Pin_1, J2.pulse
  GND_2: U2.Pin_3, U3.Pin_4, R5.Pin_1, Componente3.GND, J1.gnd, J1.pulse, J2.gnd
  N10: U3.Pin_2, R4.Pin_0
  N11: R5.Pin_0, Componente3.+

custom parts:
  ESP32S-HiLetgo: HiLetgo ESP-WROOM-32 ESP32 ESP-32S Development Board 2.4GHz Dual-Mode WiFi + Bluetooth Dual Cores Microcontroller The ESP32 integrated with Antenna switches, RF Balun, power amplifiers, low-noise amplifiers, filters, and management modules, and the entire solution occupies the least area of PCB. 2.4 GHz Wi-Fi plus Bluetooth dual-mode chip, with TSMC Ultra-low power consumption 40nm technology,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
  Adafruit INA3221 - Triple 0-26 VDC, ±3.2 Amp Power Monitor - STEMMA QT / Qwiic: This breakout board will solve all your multi-rail power-monitoring problems. Instead of struggling with up to 6 multimeters, you can just use the handy INA3221 chip on this breakout to both measure both the high side voltage and DC current draw of up to three power supplies over I2C with ±1% precision. Most current-measuring devices such as our current panel meter are only good for low side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
  GY-NEO6MV2: Description: Module GPS , type GY-NEO6MV2, pour arduino et autres micro-contrôleurs. Caractéristiques De type GY-NEO6MV2 Alimentation 3V-5V Avec Flight Control EEPROM MWC Antenne large céramique, fort signal, 25 x 25 mm Paramètres de configuration sauvegardés en EEPROM Avec batterie de backup de données LED témoin de signal Module miniaturisé 25 x 35 mm Trou de fixation de 3mm Baud rate par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
